# Fritzing sketch Fritzing-sch (saved by Fritzing 0.9.3b)

parts:
  Digispark1 = Digispark
  HC-SR04_Sensor_1 = HC-SR04 Ultrasonic Distance Sensor
  J1 = Piezo Speaker

nets:
  VCC: Digispark1.VCC, HC-SR04_Sensor_1.VCC, J1.pin2
  GND: Digispark1.GND, HC-SR04_Sensor_1.GND, J1.pin1
  N1: Digispark1.P0, HC-SR04_Sensor_1.ECHO
  N2: Digispark1.P1, HC-SR04_Sensor_1.TRIG

custom parts:
  Digispark: The Digispark is an Attiny85 based microcontroller development board similar to the Arduino line, only cheaper, smaller, and a bit less powerful. With a whole host of shields to extend its functionality and the ability to use the familiar Arduino IDE the Digispark is a great way to jump into electronics, or perfect for when an Arduino is too big or too much.
